# Fritzing sketch temp_sensor_DD (saved by Fritzing 0.9.3b)
breadboards: 1

parts:
  DHT1 = DHT11 Humitidy and Temperature Sensor
  Componente1 = Arduino Uno (Rev3)

nets:
  VDD: DHT1.VDD, Componente1.5V
  N1: DHT1.DATA, Componente1.D6_PWM
  GND: DHT1.GND, Componente1.GND

custom parts:
  DHT11 Humitidy and Temperature Sensor: DHT11 Humidity and Temperature Sensor

// code stored in the sketch: tsdd.ino
#include "DHT.h" // lib para mod temp
#define DHTPIN 6 // pin de comunicacion con el sensor de temperatura
#define DHTTYPE DHT11 // referencia del sensor


DHT dht(DHTPIN,DHTTYPE); // instancia de objeto de clase DHT

void setup() {
  Serial.begin(9600);
  Serial.println("Probando conexion con sensor de temperatura");
  dht.begin(); // inicializamos el obj
 
}

void loop() {
  delay(2000);

  //temperatura
  float humedad = dht.readHumidity();
  float temperatura = dht.readTemperature();
  float hic = dht.computeHeatIndex(temperatura, humedad, false); // sensacion termica en C°

  if (isnan(humedad)|| isnan(temperatura)){
    Serial.println("Error al leer del sensor");
    return;
  }

  
  delay(350);
  Serial.print("Humedad: ");
  Serial.print(humedad);
  Serial.print("%   ");
  Serial.print("Temperatura: ");
  Serial.print(temperatura);
  Serial.print("°C  ");
  Serial.print("Sensación termica: ");
  Serial.print(hic);
  Serial.print("°C  ");
  Serial.println();
   
}
